// Logisim project Registrador de 4bits.circ as structural Verilog: 2 circuits, main circuit main
module main (
  input  D,
  input  CLK,
  output Q
);

  wire nand_1_out, nand_2_out, nand_4_out, not_1_out;

  not not_1 (not_1_out, D);
  nand nand_1 (nand_1_out, D, CLK);
  nand nand_2 (nand_2_out, CLK, not_1_out);
  nand nand_3 (Q, nand_1_out, nand_4_out);
  nand nand_4 (nand_4_out, Q, nand_2_out);
endmodule

module FlipFlopD (
  input  in_1,
  input  in_2,
  input  in_3,
  input  in_4,
  input  CLK,
  output out_6,
  output out_7,
  output out_8,
  output out_9
);

  main main_1 (.D(in_1), .CLK(CLK), .Q(out_6));
  main main_2 (.D(in_2), .CLK(CLK), .Q(out_7));
  main main_3 (.D(in_3), .CLK(CLK), .Q(out_8));
  main main_4 (.D(in_4), .CLK(CLK), .Q(out_9));

  // Notes on the sheet:
  //   4 bit's de entrada
  //   4bit's de saida
endmodule
